# Fritzing sketch A33_Fritzing (saved by Fritzing 0.9.10b)
circuit board: 8.46667cm x 5.64444cm
breadboards: 1

parts:
  S1 = Momentary Switch [package=ksa_sealed_tac_switch]
  OLED1 = OLED 128x64 I2C Monochrome Display
  R1 = Resistor [tolerance=±5% power=0.25 resistance=10k package=THT]
  BAT1 = Battery Holders [package=battery-aa-kit]
  A1 = ESP32 wrover cam

nets:
  N1: S1.1, OLED1.VDD, A1.Pin_1
  N2: S1.3, R1.Pin_1, A1.Pin_13
  N3: OLED1.GND, R1.Pin_0, BAT1.-, A1.Pin_14, A1.Pin_40
  N4: OLED1.SCK, A1.Pin_8
  N5: OLED1.SDA, A1.Pin_7
  N6: BAT1.+, A1.Pin_19, A1.Pin_20

custom parts:
  ESP32 wrover cam: ESP32-WROVER -> A powerful and small controller with onboard camera and wireless.
